# Fritzing sketch SpotPi2_3 (saved by Fritzing 0.9.3b)
breadboards: 1

parts:
  JP1 = Header 6 [package=1x06_smd_straight_combo]
  JP2 = Header 6 [package=1x06_smd_straight_combo]
  U2 = MAX485 [package=dil08]
  R2 = Resistor [tolerance=±5% resistance=100 package=THT]
  Part1 = Arduino Mega 2560 (Rev3)
  Raspberry_Pi1 = Raspberry Pi B rev2
  J1 = female pin header, 2 pins [form="♀ (female)"]
  JP3 = Header 5 [package=1x05-1mm-ra]
  R3 = Resistor [tolerance=±5% resistance=2.2k package=THT]
  R4 = Resistor [tolerance=±5% resistance=3.3k package=THT]
  U3 = DC-DC_CONVERTER [part_number=LM2596 package=dc-dc_converter]
  U4 = KENT_LCD_CONN [package=ffc_16]
  Q2 = NPN-Transistor [package="TO92 [THT]"]
  R7 = Resistor [tolerance=±5% resistance=10k package=THT]
  R8 = Resistor [tolerance=±5% resistance=1k package=THT]
  D4 = Rectifier Diode [part_number=1N4148 package="300 mil [THT]"]
  D5 = Rectifier Diode [part_number=1N4148 package="300 mil [THT]"]
  Pad1 = Pad [width=7.902222222222222 height=9.0311111111111106 connect=center]  # not connected
  JP4 = Header 2 [package=jst-2-pth-kit]
  LED1 = LED - 5mm [color="Red (633nm)" package="5 mm [THT]"]
  R9 = Resistor [tolerance=±5% resistance=2.2k package=THT]
  Q3 = LTR-301 [part_number=PT333 package=ltr-301]
  R10 = Resistor [tolerance=±5% resistance=6.8k package=THT]

nets:
  N1: JP1.1, J1.pin2
  N2: JP1.2, JP3.5
  N3: JP1.3, JP3.4
  N4: JP1.4, JP3.3
  N5: JP1.5, U2.B
  N6: JP1.6, J1.pin1
  N7: JP2.1, JP3.1
  N8: JP2.4, U2.A
  N9: JP2.5, JP3.2
  N10: U2.RO, Part1.D19/RX1
  N11: U2.RE, U2.DE, Part1.D28
  N12: U2.DI, Part1.D18/TX1
  Yellow: R2.Pin_0
  N13: Part1.SCL, Raspberry_Pi1.GPIO_3
  N14: Part1.SDA, Raspberry_Pi1.GPIO_2
  N15: Part1.D8_PWM, R3.Pin_1
  GND: Part1.GND, Raspberry_Pi1.GND, U4._RESET
  N16: Raspberry_Pi1.GPIO_17, R3.Pin_0, R4.Pin_1
  N17: Raspberry_Pi1.GPIO_18, U4.NC1
  N18: Raspberry_Pi1.GPIO_10, U4.SI
  N19: Raspberry_Pi1.GPIO_11, U4.SCK
  N20: Raspberry_Pi1.GPIO_8, U4.CS
  GND_2: R4.Pin_0, U3.GND1, Q2.E, LED1.cathode, R10.Pin_0
  N21: U3.ON_OFF, Q2.C, R7.Pin_0
  N22: U3.VIN, R7.Pin_1
  N23: Q2.B, R8.Pin_1
  N24: R8.Pin_0, D4.cathode, D5.cathode
  N25: D4.anode, JP4.2, Q3.E, R10.Pin_1
  N26: LED1.anode, R9.Pin_0
  12V: Q3.C

notes:
  Constant +12V( Not connected)
  +8,8V when radio on
  Radio connector
  Rpi Gpio 27 output. Uses dtoverlay on Ggpio27 which turns low when Rpi has shut down
  Stiftlist.Gnd(närmast skruvterminal).Gpio9.Gpio27.Cd Enable.
  Radio on - relay on. Rpi holds the relay high via D1 to be able to make a clean shutdown.
  3V3 when radio on
  Gpio 9 detects when radio is on
  Gpio 27 shall be high as long as the Rpi is running
